# Fritzing sketch AM2320 (saved by Fritzing 0.9.3b)

parts:
  Part1 = Arduino Uno (Rev3) - ICSP
  AM1 = AM2320 Humidity and Temperature Sensor [part_number="Adafruit #3721"]

nets:
  N1: Part1.A4/SDA, AM1.SDA
  N2: Part1.A5/SCL, AM1.SCL
  5V: Part1.5V, AM1.VDD
  GND: Part1.GND, AM1.GND

custom parts:
  AM2320 Humidity and Temperature Sensor: AM2320 I2C Humidity and Temperature Sensor
